# Fritzing sketch v2 (saved by Fritzing 0.9.1b)

parts:
  CC3K1 = Adafruit CC3000 WiFi Breakout
  Part1 = Arduino Mega 2560 (Rev3)
  DHT1 = DHT22 Humidity and Temperature Sensor
  dog1 = Watchdog [package="DIP (Dual Inline) [THT]"]

nets:
  VIN: CC3K1.VIN, Part1.5V, DHT1.VDD, dog1.power
  N1: CC3K1.CLK, Part1.D52
  N2: CC3K1.MISO, Part1.D50
  N3: CC3K1.MOSI, Part1.D51
  N4: CC3K1.CS, Part1.D48
  N5: CC3K1.VBEN, Part1.D49
  N6: CC3K1.IRQ, Part1.D19/RX1
  N7: Part1.RESET, dog1.reset
  N8: Part1.D46, DHT1.DATA, DHT1.NULL
  N9: Part1.D47, dog1.input
  GND: Part1.GND, DHT1.GND, dog1.gnd

custom parts:
  Adafruit CC3000 WiFi Breakout: CC3000 WiFi Breakout
  Watchdog: watchdog
